# Fritzing sketch schematic (saved by Fritzing 0.9.6b)
breadboards: 1

parts:
  Pro_Micro = SparkFun Pro Micro
  Button0 = Pushbutton [package="[SMD]"]
  Button1 = Pushbutton [package="[SMD]"]
  Display = OLED Mono 0.56 inch blue or white

nets:
  GND: Pro_Micro.GND, Button0.Pin_1, Button0.Pin_2, Button1.Pin_1, Button1.Pin_2, Display.GND
  N1: Pro_Micro.2, Display.SDA
  N2: Pro_Micro.3, Pro_Micro.4, Display.SCL
  N3: Pro_Micro.5, Button0.Pin_3, Button0.Pin_4
  VCC: Pro_Micro.VCC, Display.VCC
  N4: Button1.Pin_3, Button1.Pin_4

notes:
  Connect this wire to ground to reset the Pro Micro (I'm too lazy to wire another button)

custom parts:
  SparkFun Pro Micro: The Pro Micro is similar to the Pro Mini except with an ATmega32U4 on board. The USB transceiver inside the 32U4 allows us to add USB connectivity on-board and do away with bulky external USB interface. Based on: https://github.com/unorthodox-engineers/unorthodox-arduino/blob/master/Unorthodox/fritzing/parts/Pro%20Micro.fzpz
  OLED Mono 0.56 inch blue or white: OLED, I2C 3.3V - 5V Blue and White text versions
